# Fritzing sketch GENIUS (saved by Fritzing 0.9.2b)
breadboards: 1

parts:
  LED1 = smd LED [color="Blue (430nm)" package="1206 [SMD]"]
  R1 = Resistor [tolerance=±5% resistance=220 package="1206 [SMD]"]
  LED2 = smd LED [color="Green (555nm)" package="1206 [SMD]"]
  R2 = Resistor [tolerance=±5% resistance=220 package="1206 [SMD]"]
  S2 = Pushbutton [package="[SMD]"]
  LED3 = smd LED [color="Red (633nm)" package="1206 [SMD]"]
  R3 = Resistor [tolerance=±5% resistance=220 package="1206 [SMD]"]
  S3 = Pushbutton [package="[SMD]"]
  S1 = Pushbutton [package="[SMD]"]
  Componente1 = Arduino Uno (Rev3)
  J1 = Piezo Speaker
  7_Segment1 = 7 Segment Display
  R5 = Resistor [tolerance=±5% resistance=220 package="1206 [SMD]"]
  LCD1 = LCD screen
  LCM1602_IIC1 = LCM1602 IIC [part_number="LCM1602 IIC" chip_label="LCM1602 IIC" package="DIP (Dual Inline) [THT]"]
  U2 = 74HC4052 [package=dil16]
  T1 = LM35 Temperature Sensor [package="TO92 [THT]"]
  LED4 = smd LED [color="Yellow (595nm)" package="1206 [SMD]"]
  S4 = Pushbutton [package="[SMD]"]
  L6 = Photocell (LDR) [package=THT]
  R4 = Resistor [tolerance=±5% resistance=220 package="1206 [SMD]"]
  R6 = Resistor [tolerance=±5% resistance=10 package="1206 [SMD]"]

nets:
  N1: LED1.cathode, R1.Pin_0
  N2: LED1.anode, Componente1.D9_PWM
  GND: R1.Pin_1, R2.Pin_1, S2.Pin_3, S2.Pin_4, R3.Pin_1, S3.Pin_3, S3.Pin_4, S1.Pin_3, S1.Pin_4, Componente1.GND, J1.pin1, R5.Pin_1, LCM1602_IIC1.GND, U2.Y1, U2.GND, T1.GND, S4.Pin_3, S4.Pin_4, R4.Pin_1, R6.Pin_1
  N3: LED2.cathode, R2.Pin_0
  N4: LED2.anode, Componente1.D10_PWM/SS
  N5: S2.Pin_1, S2.Pin_2, Componente1.D6_PWM
  N6: LED3.cathode, R3.Pin_0
  N7: LED3.anode, Componente1.D11_PWM/MOSI
  N8: S3.Pin_1, S3.Pin_2, Componente1.D7
  N9: S1.Pin_1, S1.Pin_2, Componente1.D5_PWM
  N10: Componente1.A0, U2.VEE
  N11: Componente1.A1, U2.Y0
  N12: Componente1.A2, L6.pin_0, R6.Pin_0
  N13: Componente1.A3, T1.Vout
  N14: Componente1.A4/SDA, Componente1.A5/SCL, LCM1602_IIC1.SDA, LCM1602_IIC1.SCL
  N15: Componente1.D8, S4.Pin_1, S4.Pin_2
  N16: Componente1.D12/MISO, LED4.anode
  N17: Componente1.D13/SCK, J1.pin2
  N18: Componente1.D2, U2.Y2
  N19: Componente1.D3_PWM, U2.INH
  VCC: Componente1.5V, LCM1602_IIC1.VCC, U2.Y, U2.Y3, U2.VCC, T1.+Vs, L6.pin_1
  N20: 7_Segment1.Segment_E, U2.B
  N21: 7_Segment1.Segment_D, U2.A
  N22: 7_Segment1.common_cathode, R5.Pin_0
  N23: 7_Segment1.Segment_C, U2.X3
  N24: 7_Segment1.Segment_B, U2.X0
  N25: 7_Segment1.Segment_A, U2.X
  N26: 7_Segment1.Segment_F, U2.X2
  N27: 7_Segment1.Segment_G, U2.X1
  VSS: LCD1.VSS, LCM1602_IIC1.VSS
  VDD: LCD1.VDD, LCM1602_IIC1.VDD
  N28: LCD1.V0, LCM1602_IIC1.V0
  N29: LCD1.RS, LCM1602_IIC1.RS
  N30: LCD1.R/W, LCM1602_IIC1.RW
  N31: LCD1.E, LCM1602_IIC1.E
  N32: LCD1.DB0, LCM1602_IIC1.D0
  N33: LCD1.DB1, LCM1602_IIC1.D1
  N34: LCD1.DB2, LCM1602_IIC1.D2
  N35: LCD1.DB3, LCM1602_IIC1.D3
  N36: LCD1.DB4, LCM1602_IIC1.D4
  N37: LCD1.DB5, LCM1602_IIC1.D5
  N38: LCD1.DB6, LCM1602_IIC1.D6
  N39: LCD1.DB7, LCM1602_IIC1.D7
  N40: LCD1.LED+, LCM1602_IIC1.A
  N41: LCD1.LED-, LCM1602_IIC1.K
  N42: LED4.cathode, R4.Pin_0

notes:
  Powered By Decade Technologies

custom parts:
  LCM1602 IIC: I2C-Module to use a 1602 or 2004 LCD on with the wire.h libory Serial LCD Modul

// code stored in the sketch: GENIUS.ino
#include <Wire.h>
#include <LiquidCrystal_I2C.h>

LiquidCrystal_I2C lcd(0x20, 2, 1, 0, 4, 5, 6, 7, 3, POSITIVE);

#define RED_BUTTON 2
#define GREEN_BUTTON 3
#define BLUE_BUTTON 4
#define YELLOW_BUTTON 5

#define RED_LED 8
#define GREEN_LED 9
#define BLUE_LED 10
#define YELLOW_LED 11

#define DEFAULT_BUZZER 13

#define BINARY_SEGMENT1 14
#define BINARY_SEGMENT2 15
#define BINARY_SEGMENT3 16
#define BINARY_SEGMENT4 17

const int MAX_SEQUENCE = 4;
const int HOLD_ON = 500;
const int UNDEFINIED = -1;

int gameSet[MAX_SEQUENCE];
int roundPlayer;
int rightAnswer;

enum statusGame {
  READY_TO_PLAY
, WAITING_RESPONSE
, YOU_WIN
, GAME_OVER
};

void setDisplayMessage(String text) {
  lcd.clear();

  //lcd.setBacklight(HIGH);
  lcd.setCursor(0, 0);
  lcd.print(text);
  lcd.setCursor(0, 1);
  lcd.print("decade.com.br");
  lcd.setBacklight(LOW);
}

void setDisplayColor(int ledPort) {
  switch (ledPort) {
    case RED_LED:
      setDisplayMessage("RED (VERMELHO)");

      break;
    case GREEN_LED:
      setDisplayMessage("GREEN (VERDE)");

      break;
    case BLUE_LED:
      setDisplayMessage("WHITE (BRANCO)");

      break;
    case YELLOW_LED:
      setDisplayMessage("YELLOW (AMARELO)");

      break;
  }
}

void setDisplayNumber(int number) {
  switch (number) {
    case 0:
      digitalWrite(BINARY_SEGMENT1, LOW);
      digitalWrite(BINARY_SEGMENT2, LOW);
      digitalWrite(BINARY_SEGMENT3, LOW);
      digitalWrite(BINARY_SEGMENT4, LOW);

      break;
    case 1:
      digitalWrite(BINARY_SEGMENT1, HIGH);
      digitalWrite(BINARY_SEGMENT2, LOW);
      digitalWrite(BINARY_SEGMENT3, LOW);
      digitalWrite(BINARY_SEGMENT4, LOW);

      break;
    case 2:
      digitalWrite(BINARY_SEGMENT1, LOW);
      digitalWrite(BINARY_SEGMENT2, HIGH);
      digitalWrite(BINARY_SEGMENT3, LOW);
      digitalWrite(BINARY_SEGMENT4, LOW);

      break;
    case 3:
      digitalWrite(BINARY_SEGMENT1, HIGH);
      digitalWrite(BINARY_SEGMENT2, HIGH);
      digitalWrite(BINARY_SEGMENT3, LOW);
      digitalWrite(BINARY_SEGMENT4, LOW);

      break;
    case 4:
      digitalWrite(BINARY_SEGMENT1, LOW);
      digitalWrite(BINARY_SEGMENT2, LOW);
      digitalWrite(BINARY_SEGMENT3, HIGH);
      digitalWrite(BINARY_SEGMENT4, LOW);

      break;
    case 5:
      digitalWrite(BINARY_SEGMENT1, HIGH);
      digitalWrite(BINARY_SEGMENT2, LOW);
      digitalWrite(BINARY_SEGMENT3, HIGH);
      digitalWrite(BINARY_SEGMENT4, LOW);

      break;
    case 6:
      digitalWrite(BINARY_SEGMENT1, LOW);
      digitalWrite(BINARY_SEGMENT2, HIGH);
      digitalWrite(BINARY_SEGMENT3, HIGH);
      digitalWrite(BINARY_SEGMENT4, LOW);

      break;
    case 7:
      digitalWrite(BINARY_SEGMENT1, HIGH);
      digitalWrite(BINARY_SEGMENT2, HIGH);
      digitalWrite(BINARY_SEGMENT3, HIGH);
      digitalWrite(BINARY_SEGMENT4, LOW);

      break;
    case 8:
      digitalWrite(BINARY_SEGMENT1, LOW);
      digitalWrite(BINARY_SEGMENT2, LOW);
      digitalWrite(BINARY_SEGMENT3, LOW);
      digitalWrite(BINARY_SEGMENT4, HIGH);

      break;
    case 9:
      digitalWrite(BINARY_SEGMENT1, HIGH);
      digitalWrite(BINARY_SEGMENT2, LOW);
      digitalWrite(BINARY_SEGMENT3, LOW);
      digitalWrite(BINARY_SEGMENT4, HIGH);

      break;
  }
}

void setPlayTone(int frequence, int duration) {
  tone(DEFAULT_BUZZER, frequence, duration);
}

void setFlashLight(int ledPort, int waitingTime) {
  digitalWrite(ledPort, HIGH);
  delay(waitingTime);

  setPlayTone(ledPort * 512, 128);

  digitalWrite(ledPort, LOW);
  delay(waitingTime);
}

int getButtonPressed() {
  if (digitalRead(RED_BUTTON) == LOW) {
    setDisplayColor(RED_LED);
    setFlashLight(RED_LED, HOLD_ON);
    setDisplayMessage("NEXT COLOR");

    return RED_LED;
  }

  if (digitalRead(GREEN_BUTTON) == LOW) {
    setDisplayColor(GREEN_LED);
    setFlashLight(GREEN_LED, HOLD_ON);
    setDisplayMessage("NEXT COLOR");

    return GREEN_LED;
  }

  if (digitalRead(BLUE_BUTTON) == LOW) {
    setDisplayColor(BLUE_LED);
    setFlashLight(BLUE_LED, HOLD_ON);
    setDisplayMessage("NEXT COLOR");

    return BLUE_LED;
  }

  if (digitalRead(YELLOW_BUTTON) == LOW) {
    setDisplayColor(YELLOW_LED);
    setFlashLight(YELLOW_LED, HOLD_ON);
    setDisplayMessage("NEXT COLOR");

    return YELLOW_LED;
  }

  return UNDEFINIED;
}

void playRoundSequence() {
  setDisplayNumber(roundPlayer);

  for (int i = 0; i < roundPlayer; i++) {
    setDisplayColor(gameSet[i]);

    setFlashLight(gameSet[i], HOLD_ON);

    setDisplayMessage("PLAY SEQUENCE");
  }
}

void setRoundPlayer() {
  roundPlayer++;
  rightAnswer = 0;

  if (roundPlayer <= MAX_SEQUENCE) {
    playRoundSequence();
  }
}

void setRightAnswer() {
  int answer = getButtonPressed();

  if (answer == UNDEFINIED) {
    return;
  }

  if (answer == gameSet[rightAnswer]) {
    rightAnswer++;
  } else {
    roundPlayer = MAX_SEQUENCE + 2;
  }
}

int getStatusGame() {
  if (roundPlayer <= MAX_SEQUENCE) {
    if (rightAnswer == roundPlayer) {
      return READY_TO_PLAY;
    } else {
      return WAITING_RESPONSE;
    }
  } else if (roundPlayer == MAX_SEQUENCE + 1) {
    return YOU_WIN;
  } else {
    return GAME_OVER;
  }
}

void welcome() {
  digitalWrite(RED_LED, HIGH);
  digitalWrite(GREEN_LED, HIGH);
  digitalWrite(BLUE_LED, HIGH);
  digitalWrite(YELLOW_LED, HIGH);

  delay(400);

  digitalWrite(RED_LED, LOW);
  digitalWrite(GREEN_LED, LOW);
  digitalWrite(BLUE_LED, LOW);
  digitalWrite(YELLOW_LED, LOW);

  delay(400);
}

void congratulation() {
  setDisplayMessage("YOU WIN!");

  for (int i = 0; i < MAX_SEQUENCE + 1; i++) {
    setFlashLight(gameSet[i], 200);

    setDisplayNumber(MAX_SEQUENCE);
  }

  newGame();
}

void fail() {
  setDisplayMessage("YOU LOOSE!");

  setPlayTone(2048, 256);

  digitalWrite(RED_LED, HIGH);
  digitalWrite(GREEN_LED, HIGH);
  digitalWrite(BLUE_LED, HIGH);
  digitalWrite(YELLOW_LED, HIGH);

  setDisplayNumber(0);

  delay(300);

  newGame();
}

void newGame() {
  roundPlayer = 0;
  rightAnswer = 0;

  randomSeed(analogRead(A7));

  for (int i = 0; i < MAX_SEQUENCE; i++) {
    gameSet[i] = random(RED_LED, YELLOW_LED + 1);
  }

  welcome();
}

void setup() {
  //Serial.begin(9600);

  pinMode(RED_BUTTON, INPUT_PULLUP);
  pinMode(GREEN_BUTTON, INPUT_PULLUP);
  pinMode(BLUE_BUTTON, INPUT_PULLUP);
  pinMode(YELLOW_BUTTON, INPUT_PULLUP);

  pinMode(RED_LED, OUTPUT);
  pinMode(GREEN_LED, OUTPUT);
  pinMode(BLUE_LED, OUTPUT);
  pinMode(YELLOW_LED, OUTPUT);

  pinMode(DEFAULT_BUZZER, OUTPUT);

  pinMode(BINARY_SEGMENT1, OUTPUT);
  pinMode(BINARY_SEGMENT2, OUTPUT);
  pinMode(BINARY_SEGMENT3, OUTPUT);
  pinMode(BINARY_SEGMENT4, OUTPUT);

  lcd.begin (16, 2);

  setDisplayMessage("WELCOME GAMER");

  newGame();
}

void loop() {
  switch (getStatusGame()) {
    case READY_TO_PLAY:
      //Serial.println("READY_TO_PLAY");

      setRoundPlayer();
      break;
    case WAITING_RESPONSE:
      //Serial.println("WAITING_RESPONSE");

      setRightAnswer();
      break;
    case YOU_WIN:
      //Serial.println("YOU_WIN");

      congratulation();
      break;
    case GAME_OVER:
      //Serial.println("GAME_OVER");

      fail();
      break;
  }
}

// code stored in the sketch: GENIUSv2.ino
#include <Wire.h>
#include <LiquidCrystal_I2C.h>

LiquidCrystal_I2C lcd(0x20, 2, 1, 0, 4, 5, 6, 7, 3, POSITIVE);

#define RED_BUTTON 2
#define GREEN_BUTTON 3
#define BLUE_BUTTON 4
#define YELLOW_BUTTON 5

#define RED_LED 8
#define GREEN_LED 9
#define BLUE_LED 10
#define YELLOW_LED 11

#define DEFAULT_BUZZER 13

#define BINARY_SEGMENT1 14
#define BINARY_SEGMENT2 15
#define BINARY_SEGMENT3 16
#define BINARY_SEGMENT4 17

const int MAX_SEQUENCE = 4;
const int HOLD_ON = 500;
const int UNDEFINIED = -1;

int gameSet[MAX_SEQUENCE];
int roundPlayer;
int rightAnswer;

enum statusGame {
  READY_TO_PLAY
, WAITING_RESPONSE
, YOU_WIN
, GAME_OVER
};

void setDisplayMessage(String text) {
  lcd.clear();

  //lcd.setBacklight(HIGH);
  lcd.setCursor(0, 0);
  lcd.print(text);
  lcd.setCursor(0, 1);
  lcd.print("decade.com.br");
  lcd.setBacklight(LOW);
}

void setDisplayColor(int ledPort) {
  switch (ledPort) {
    case RED_LED:
      setDisplayMessage("RED (VERMELHO)");

      break;
    case GREEN_LED:
      setDisplayMessage("GREEN (VERDE)");

      break;
    case BLUE_LED:
      setDisplayMessage("WHITE (BRANCO)");

      break;
    case YELLOW_LED:
      setDisplayMessage("YELLOW (AMARELO)");

      break;
  }
}

void setDisplayNumber(int number) {
  switch (number) {
    case 0:
      digitalWrite(BINARY_SEGMENT1, LOW);
      digitalWrite(BINARY_SEGMENT2, LOW);
      digitalWrite(BINARY_SEGMENT3, LOW);
      digitalWrite(BINARY_SEGMENT4, LOW);

      break;
    case 1:
      digitalWrite(BINARY_SEGMENT1, HIGH);
      digitalWrite(BINARY_SEGMENT2, LOW);
      digitalWrite(BINARY_SEGMENT3, LOW);
      digitalWrite(BINARY_SEGMENT4, LOW);

      break;
    case 2:
      digitalWrite(BINARY_SEGMENT1, LOW);
      digitalWrite(BINARY_SEGMENT2, HIGH);
      digitalWrite(BINARY_SEGMENT3, LOW);
      digitalWrite(BINARY_SEGMENT4, LOW);

      break;
    case 3:
      digitalWrite(BINARY_SEGMENT1, HIGH);
      digitalWrite(BINARY_SEGMENT2, HIGH);
      digitalWrite(BINARY_SEGMENT3, LOW);
      digitalWrite(BINARY_SEGMENT4, LOW);

      break;
    case 4:
      digitalWrite(BINARY_SEGMENT1, LOW);
      digitalWrite(BINARY_SEGMENT2, LOW);
      digitalWrite(BINARY_SEGMENT3, HIGH);
      digitalWrite(BINARY_SEGMENT4, LOW);

      break;
    case 5:
      digitalWrite(BINARY_SEGMENT1, HIGH);
      digitalWrite(BINARY_SEGMENT2, LOW);
      digitalWrite(BINARY_SEGMENT3, HIGH);
      digitalWrite(BINARY_SEGMENT4, LOW);

      break;
    case 6:
      digitalWrite(BINARY_SEGMENT1, LOW);
      digitalWrite(BINARY_SEGMENT2, HIGH);
      digitalWrite(BINARY_SEGMENT3, HIGH);
      digitalWrite(BINARY_SEGMENT4, LOW);

      break;
    case 7:
      digitalWrite(BINARY_SEGMENT1, HIGH);
      digitalWrite(BINARY_SEGMENT2, HIGH);
      digitalWrite(BINARY_SEGMENT3, HIGH);
      digitalWrite(BINARY_SEGMENT4, LOW);

      break;
    case 8:
      digitalWrite(BINARY_SEGMENT1, LOW);
      digitalWrite(BINARY_SEGMENT2, LOW);
      digitalWrite(BINARY_SEGMENT3, LOW);
      digitalWrite(BINARY_SEGMENT4, HIGH);

      break;
    case 9:
      digitalWrite(BINARY_SEGMENT1, HIGH);
      digitalWrite(BINARY_SEGMENT2, LOW);
      digitalWrite(BINARY_SEGMENT3, LOW);
      digitalWrite(BINARY_SEGMENT4, HIGH);

      break;
  }
}

void setPlayTone(int frequence, int duration) {
  tone(DEFAULT_BUZZER, frequence, duration);
}

void setFlashLight(int ledPort, int waitingTime) {
  digitalWrite(ledPort, HIGH);
  delay(waitingTime);

  setPlayTone(ledPort * 512, 128);

  digitalWrite(ledPort, LOW);
  delay(waitingTime);
}

int getButtonPressed() {
  if (digitalRead(RED_BUTTON) == LOW) {
    setDisplayColor(RED_LED);
    setFlashLight(RED_LED, HOLD_ON);
    setDisplayMessage("NEXT COLOR");

    return RED_LED;
  }

  if (digitalRead(GREEN_BUTTON) == LOW) {
    setDisplayColor(GREEN_LED);
    setFlashLight(GREEN_LED, HOLD_ON);
    setDisplayMessage("NEXT COLOR");

    return GREEN_LED;
  }

  if (digitalRead(BLUE_BUTTON) == LOW) {
    setDisplayColor(BLUE_LED);
    setFlashLight(BLUE_LED, HOLD_ON);
    setDisplayMessage("NEXT COLOR");

    return BLUE_LED;
  }

  if (digitalRead(YELLOW_BUTTON) == LOW) {
    setDisplayColor(YELLOW_LED);
    setFlashLight(YELLOW_LED, HOLD_ON);
    setDisplayMessage("NEXT COLOR");

    return YELLOW_LED;
  }

  return UNDEFINIED;
}

void playRoundSequence() {
  setDisplayNumber(roundPlayer);

  for (int i = 0; i < roundPlayer; i++) {
    setDisplayColor(gameSet[i]);

    setFlashLight(gameSet[i], HOLD_ON);

    setDisplayMessage("PLAY SEQUENCE");
  }
}

void setRoundPlayer() {
  roundPlayer++;
  rightAnswer = 0;

  if (roundPlayer <= MAX_SEQUENCE) {
    playRoundSequence();
  }
}

void setRightAnswer() {
  int answer = getButtonPressed();

  if (answer == UNDEFINIED) {
    return;
  }

  if (answer == gameSet[rightAnswer]) {
    rightAnswer++;
  } else {
    roundPlayer = MAX_SEQUENCE + 2;
  }
}

int getStatusGame() {
  if (roundPlayer <= MAX_SEQUENCE) {
    if (rightAnswer == roundPlayer) {
      return READY_TO_PLAY;
    } else {
      return WAITING_RESPONSE;
    }
  } else if (roundPlayer == MAX_SEQUENCE + 1) {
    return YOU_WIN;
  } else {
    return GAME_OVER;
  }
}

void welcome() {
  digitalWrite(RED_LED, HIGH);
  digitalWrite(GREEN_LED, HIGH);
  digitalWrite(BLUE_LED, HIGH);
  digitalWrite(YELLOW_LED, HIGH);

  delay(400);

  digitalWrite(RED_LED, LOW);
  digitalWrite(GREEN_LED, LOW);
  digitalWrite(BLUE_LED, LOW);
  digitalWrite(YELLOW_LED, LOW);

  delay(400);
}

void congratulation() {
  setDisplayMessage("YOU WIN!");

  for (int i = 0; i < MAX_SEQUENCE + 1; i++) {
    setFlashLight(gameSet[i], 200);

    setDisplayNumber(MAX_SEQUENCE);
  }

  newGame();
}

void fail() {
  setDisplayMessage("YOU LOOSE!");

  setPlayTone(2048, 256);

  digitalWrite(RED_LED, HIGH);
  digitalWrite(GREEN_LED, HIGH);
  digitalWrite(BLUE_LED, HIGH);
  digitalWrite(YELLOW_LED, HIGH);

  setDisplayNumber(0);

  delay(300);

  newGame();
}

void newGame() {
  roundPlayer = 0;
  rightAnswer = 0;

  randomSeed(analogRead(A7));

  for (int i = 0; i < MAX_SEQUENCE; i++) {
    gameSet[i] = random(RED_LED, YELLOW_LED + 1);
  }

  welcome();
}

void setup() {
  //Serial.begin(9600);

  pinMode(RED_BUTTON, INPUT_PULLUP);
  pinMode(GREEN_BUTTON, INPUT_PULLUP);
  pinMode(BLUE_BUTTON, INPUT_PULLUP);
  pinMode(YELLOW_BUTTON, INPUT_PULLUP);

  pinMode(RED_LED, OUTPUT);
  pinMode(GREEN_LED, OUTPUT);
  pinMode(BLUE_LED, OUTPUT);
  pinMode(YELLOW_LED, OUTPUT);

  pinMode(DEFAULT_BUZZER, OUTPUT);

  pinMode(BINARY_SEGMENT1, OUTPUT);
  pinMode(BINARY_SEGMENT2, OUTPUT);
  pinMode(BINARY_SEGMENT3, OUTPUT);
  pinMode(BINARY_SEGMENT4, OUTPUT);

  lcd.begin (16, 2);

  setDisplayMessage("WELCOME GAMER");

  newGame();
}

void loop() {
  switch (getStatusGame()) {
    case READY_TO_PLAY:
      //Serial.println("READY_TO_PLAY");

      setRoundPlayer();
      break;
    case WAITING_RESPONSE:
      //Serial.println("WAITING_RESPONSE");

      setRightAnswer();
      break;
    case YOU_WIN:
      //Serial.println("YOU_WIN");

      congratulation();
      break;
    case GAME_OVER:
      //Serial.println("GAME_OVER");

      fail();
      break;
  }
}

// code stored in the sketch: GENIUSv3.ino
#include <Wire.h>
#include <LiquidCrystal_I2C.h>

LiquidCrystal_I2C lcd(0x20, 2, 1, 0, 4, 5, 6, 7, 3, POSITIVE);

#define BINARY_SEGMENT1 2
#define BINARY_SEGMENT2 3
#define BINARY_SEGMENT3 14
#define BINARY_SEGMENT4 15

#define BLUE_BUTTON 5
#define GREEN_BUTTON 6
#define RED_BUTTON 7
#define YELLOW_BUTTON 8

#define BLUE_LED 9
#define GREEN_LED 10
#define RED_LED 11
#define YELLOW_LED 12

#define DEFAULT_BUZZER 13

#define LDR 16
#define LM35 17

const int MAX_SEQUENCE = 9;
const int HOLD_ON = 500;
const int UNDEFINIED = -1;

int gameSet[MAX_SEQUENCE];
int roundPlayer;
int rightAnswer;

enum statusGame {
  READY_TO_PLAY
, WAITING_RESPONSE
, YOU_WIN
, GAME_OVER
};

void setDisplayMessage(String line1, String line2) {
  float weatherNow = analogRead(LM35) * 0.1075268817;

  line1 = (line1=="")?"WELCOME GAMER":line1;
  line2 = (line2=="")?"Weather Now: " + String((int) weatherNow) + "c":line2;

  lcd.clear();

  lcd.setCursor(0, 0);
  lcd.print(line1);
  lcd.setCursor(0, 1);
  lcd.print(line2);
}

void setDisplaySegment(int number) {
  switch (number) {
    case 0:
      digitalWrite(BINARY_SEGMENT1, LOW);
      digitalWrite(BINARY_SEGMENT2, LOW);
      digitalWrite(BINARY_SEGMENT3, LOW);
      digitalWrite(BINARY_SEGMENT4, LOW);

      break;
    case 1:
      digitalWrite(BINARY_SEGMENT1, HIGH);
      digitalWrite(BINARY_SEGMENT2, LOW);
      digitalWrite(BINARY_SEGMENT3, LOW);
      digitalWrite(BINARY_SEGMENT4, LOW);

      break;
    case 2:
      digitalWrite(BINARY_SEGMENT1, LOW);
      digitalWrite(BINARY_SEGMENT2, HIGH);
      digitalWrite(BINARY_SEGMENT3, LOW);
      digitalWrite(BINARY_SEGMENT4, LOW);

      break;
    case 3:
      digitalWrite(BINARY_SEGMENT1, HIGH);
      digitalWrite(BINARY_SEGMENT2, HIGH);
      digitalWrite(BINARY_SEGMENT3, LOW);
      digitalWrite(BINARY_SEGMENT4, LOW);

      break;
    case 4:
      digitalWrite(BINARY_SEGMENT1, LOW);
      digitalWrite(BINARY_SEGMENT2, LOW);
      digitalWrite(BINARY_SEGMENT3, HIGH);
      digitalWrite(BINARY_SEGMENT4, LOW);

      break;
    case 5:
      digitalWrite(BINARY_SEGMENT1, HIGH);
      digitalWrite(BINARY_SEGMENT2, LOW);
      digitalWrite(BINARY_SEGMENT3, HIGH);
      digitalWrite(BINARY_SEGMENT4, LOW);

      break;
    case 6:
      digitalWrite(BINARY_SEGMENT1, LOW);
      digitalWrite(BINARY_SEGMENT2, HIGH);
      digitalWrite(BINARY_SEGMENT3, HIGH);
      digitalWrite(BINARY_SEGMENT4, LOW);

      break;
    case 7:
      digitalWrite(BINARY_SEGMENT1, HIGH);
      digitalWrite(BINARY_SEGMENT2, HIGH);
      digitalWrite(BINARY_SEGMENT3, HIGH);
      digitalWrite(BINARY_SEGMENT4, LOW);

      break;
    case 8:
      digitalWrite(BINARY_SEGMENT1, LOW);
      digitalWrite(BINARY_SEGMENT2, LOW);
      digitalWrite(BINARY_SEGMENT3, LOW);
      digitalWrite(BINARY_SEGMENT4, HIGH);

      break;
    case 9:
      digitalWrite(BINARY_SEGMENT1, HIGH);
      digitalWrite(BINARY_SEGMENT2, LOW);
      digitalWrite(BINARY_SEGMENT3, LOW);
      digitalWrite(BINARY_SEGMENT4, HIGH);

      break;
  }
}

void setColorMessage(int ledPort) {
  switch (ledPort) {
    case RED_LED:
      setDisplayMessage("RED (VERMELHO)","");

      break;
    case GREEN_LED:
      setDisplayMessage("GREEN (VERDE)","");

      break;
    case BLUE_LED:
      setDisplayMessage("BLUE (AZUL)","");

      break;
    case YELLOW_LED:
      setDisplayMessage("YELLOW (AMARELO)","");

      break;
  }
}

void setPlayTone(int frequence, int duration) {
  tone(DEFAULT_BUZZER, frequence, duration);
}

void setFlashLight(int ledPort, int waitingTime) {
  digitalWrite(ledPort, HIGH);
  delay(waitingTime);

  setPlayTone(ledPort * 400, 200);

  digitalWrite(ledPort, LOW);
  delay(waitingTime);
}

int getButtonPressed() {
  if (digitalRead(RED_BUTTON) == LOW) {
    setColorMessage(RED_LED);
    setFlashLight(RED_LED, HOLD_ON);
    setDisplayMessage("NEXT COLOR","");

    return RED_LED;
  }

  if (digitalRead(GREEN_BUTTON) == LOW) {
    setColorMessage(GREEN_LED);
    setFlashLight(GREEN_LED, HOLD_ON);
    setDisplayMessage("NEXT COLOR","");

    return GREEN_LED;
  }

  if (digitalRead(BLUE_BUTTON) == LOW) {
    setColorMessage(BLUE_LED);
    setFlashLight(BLUE_LED, HOLD_ON);
    setDisplayMessage("NEXT COLOR","");

    return BLUE_LED;
  }

  if (digitalRead(YELLOW_BUTTON) == LOW) {
    setColorMessage(YELLOW_LED);
    setFlashLight(YELLOW_LED, HOLD_ON);
    setDisplayMessage("NEXT COLOR","");

    return YELLOW_LED;
  }

  return UNDEFINIED;
}

void playRoundSequence() {
  for (int i = 0; i < roundPlayer; i++) {
    setDisplaySegment(i+1);

    setColorMessage(gameSet[i]);

    setFlashLight(gameSet[i], HOLD_ON);

    setDisplayMessage("PLAY SEQUENCE","");
  }
}

void setRoundPlayer() {
  roundPlayer++;
  rightAnswer = 0;

  if (roundPlayer <= MAX_SEQUENCE) {
    playRoundSequence();
  }
}

void setRightAnswer() {
  int answer = getButtonPressed();

  if (answer == UNDEFINIED) {
    return;
  }

  if (answer == gameSet[rightAnswer]) {
    rightAnswer++;
  } else {
    roundPlayer = MAX_SEQUENCE + 2;
  }
}

int getStatusGame() {
  if (roundPlayer <= MAX_SEQUENCE) {
    if (rightAnswer == roundPlayer) {
      return READY_TO_PLAY;
    } else {
      return WAITING_RESPONSE;
    }
  } else if (roundPlayer == MAX_SEQUENCE + 1) {
    return YOU_WIN;
  } else {
    return GAME_OVER;
  }
}

void welcome() {
  digitalWrite(RED_LED, HIGH);
  digitalWrite(GREEN_LED, HIGH);
  digitalWrite(BLUE_LED, HIGH);
  digitalWrite(YELLOW_LED, HIGH);

  delay(400);

  digitalWrite(RED_LED, LOW);
  digitalWrite(GREEN_LED, LOW);
  digitalWrite(BLUE_LED, LOW);
  digitalWrite(YELLOW_LED, LOW);

  delay(400);
}

void congratulation() {
  setDisplayMessage("YOU WIN","Congratulations!");

  for (int i = 0; i < MAX_SEQUENCE + 1; i++) {
    setFlashLight(gameSet[i], 200);

    setDisplaySegment(MAX_SEQUENCE);
  }

  newGame();
}

void fail() {
  setDisplayMessage("YOU LOOSE!","Try Again...");

  setPlayTone(2048, 256);

  digitalWrite(RED_LED, HIGH);
  digitalWrite(GREEN_LED, HIGH);
  digitalWrite(BLUE_LED, HIGH);
  digitalWrite(YELLOW_LED, HIGH);

  setDisplaySegment(0);

  delay(300);

  newGame();
}

void newGame() {
  roundPlayer = 0;
  rightAnswer = 0;

  randomSeed(analogRead(A7));

  for (int i = 0; i < MAX_SEQUENCE; i++) {
    gameSet[i] = random(BLUE_LED, YELLOW_LED + 1);
  }

  welcome();
}

void setup() {
  //Serial.begin(9600);

  analogReference(INTERNAL);

  pinMode(RED_BUTTON, INPUT_PULLUP);
  pinMode(GREEN_BUTTON, INPUT_PULLUP);
  pinMode(BLUE_BUTTON, INPUT_PULLUP);
  pinMode(YELLOW_BUTTON, INPUT_PULLUP);

  pinMode(RED_LED, OUTPUT);
  pinMode(GREEN_LED, OUTPUT);
  pinMode(BLUE_LED, OUTPUT);
  pinMode(YELLOW_LED, OUTPUT);

  pinMode(BINARY_SEGMENT1, OUTPUT);
  pinMode(BINARY_SEGMENT2, OUTPUT);
  pinMode(BINARY_SEGMENT3, OUTPUT);
  pinMode(BINARY_SEGMENT4, OUTPUT);

  pinMode(DEFAULT_BUZZER, OUTPUT);

  lcd.begin (16, 2);

  setDisplayMessage("WELCOME GAMER","decade.com.br");

  newGame();
}

void loop() {
  int luminosity = map(analogRead(LDR), 0, 1023, 0, 100);

  if (luminosity < 50) {
    lcd.setBacklight(HIGH);
  } else {
    lcd.setBacklight(LOW);
  }

  switch (getStatusGame()) {
    case READY_TO_PLAY:
      //Serial.println("READY_TO_PLAY");

      setRoundPlayer();
      break;
    case WAITING_RESPONSE:
      //Serial.println("WAITING_RESPONSE");

      setRightAnswer();
      break;
    case YOU_WIN:
      //Serial.println("YOU_WIN");

      congratulation();
      break;
    case GAME_OVER:
      //Serial.println("GAME_OVER");

      fail();
      break;
  }
}

// code stored in the sketch: GENIUSv4.ino
#include <Wire.h>
#include <LiquidCrystal_I2C.h>

LiquidCrystal_I2C lcd(0x20, 2, 1, 0, 4, 5, 6, 7, 3, POSITIVE);

#define BINARY_SEGMENT1 2
#define BINARY_SEGMENT2 3
#define BINARY_SEGMENT3 14
#define BINARY_SEGMENT4 15

#define BLUE_BUTTON 5
#define GREEN_BUTTON 6
#define RED_BUTTON 7
#define YELLOW_BUTTON 8

#define BLUE_LED 9
#define GREEN_LED 10
#define RED_LED 11
#define YELLOW_LED 12

#define DEFAULT_BUZZER 13

#define LDR 16
#define LM35 17

const int MAX_SEQUENCE = 9;
const int HOLD_ON = 500;
const int UNDEFINIED = -1;

int gameSet[MAX_SEQUENCE];
int roundPlayer;
int rightAnswer;

enum statusGame {
  READY_TO_PLAY
, WAITING_RESPONSE
, YOU_WIN
, GAME_OVER
};

void setDisplayMessage(String line1, String line2) {
  float weatherNow = analogRead(LM35) * 0.1075268817;

  line1 = (line1=="")?"WELCOME GAMER":line1;
  line2 = (line2=="")?"Weather Now: " + String((int) weatherNow) + "c":line2;

  Serial.println(line1);
  Serial.println(line2);

  lcd.clear();

  lcd.setCursor(0, 0);
  lcd.print(line1);
  lcd.setCursor(0, 1);
  lcd.print(line2);
}

void setDisplaySegment(int number) {
  Serial.println(number);

  switch (number) {
    case 0:
      digitalWrite(BINARY_SEGMENT1, LOW);
      digitalWrite(BINARY_SEGMENT2, LOW);
      digitalWrite(BINARY_SEGMENT3, LOW);
      digitalWrite(BINARY_SEGMENT4, LOW);

      break;
    case 1:
      digitalWrite(BINARY_SEGMENT1, HIGH);
      digitalWrite(BINARY_SEGMENT2, LOW);
      digitalWrite(BINARY_SEGMENT3, LOW);
      digitalWrite(BINARY_SEGMENT4, LOW);

      break;
    case 2:
      digitalWrite(BINARY_SEGMENT1, LOW);
      digitalWrite(BINARY_SEGMENT2, HIGH);
      digitalWrite(BINARY_SEGMENT3, LOW);
      digitalWrite(BINARY_SEGMENT4, LOW);

      break;
    case 3:
      digitalWrite(BINARY_SEGMENT1, HIGH);
      digitalWrite(BINARY_SEGMENT2, HIGH);
      digitalWrite(BINARY_SEGMENT3, LOW);
      digitalWrite(BINARY_SEGMENT4, LOW);

      break;
    case 4:
      digitalWrite(BINARY_SEGMENT1, LOW);
      digitalWrite(BINARY_SEGMENT2, LOW);
      digitalWrite(BINARY_SEGMENT3, HIGH);
      digitalWrite(BINARY_SEGMENT4, LOW);

      break;
    case 5:
      digitalWrite(BINARY_SEGMENT1, HIGH);
      digitalWrite(BINARY_SEGMENT2, LOW);
      digitalWrite(BINARY_SEGMENT3, HIGH);
      digitalWrite(BINARY_SEGMENT4, LOW);

      break;
    case 6:
      digitalWrite(BINARY_SEGMENT1, LOW);
      digitalWrite(BINARY_SEGMENT2, HIGH);
      digitalWrite(BINARY_SEGMENT3, HIGH);
      digitalWrite(BINARY_SEGMENT4, LOW);

      break;
    case 7:
      digitalWrite(BINARY_SEGMENT1, HIGH);
      digitalWrite(BINARY_SEGMENT2, HIGH);
      digitalWrite(BINARY_SEGMENT3, HIGH);
      digitalWrite(BINARY_SEGMENT4, LOW);

      break;
    case 8:
      digitalWrite(BINARY_SEGMENT1, LOW);
      digitalWrite(BINARY_SEGMENT2, LOW);
      digitalWrite(BINARY_SEGMENT3, LOW);
      digitalWrite(BINARY_SEGMENT4, HIGH);

      break;
    case 9:
      digitalWrite(BINARY_SEGMENT1, HIGH);
      digitalWrite(BINARY_SEGMENT2, LOW);
      digitalWrite(BINARY_SEGMENT3, LOW);
      digitalWrite(BINARY_SEGMENT4, HIGH);

      break;
  }
}

void setColorMessage(int ledPort) {
  switch (ledPort) {
    case RED_LED:
      setDisplayMessage("RED (VERMELHO)","");

      break;
    case GREEN_LED:
      setDisplayMessage("GREEN (VERDE)","");

      break;
    case BLUE_LED:
      setDisplayMessage("BLUE (AZUL)","");

      break;
    case YELLOW_LED:
      setDisplayMessage("YELLOW (AMARELO)","");

      break;
  }
}

void setPlayTone(int frequence, int duration) {
  tone(DEFAULT_BUZZER, frequence, duration);
}

void setFlashLight(int ledPort, int waitingTime) {
  digitalWrite(ledPort, HIGH);
  delay(waitingTime);

  setPlayTone(ledPort * 400, 200);

  digitalWrite(ledPort, LOW);
  delay(waitingTime);
}

int getButtonPressed() {
  char keyPress = Serial.read();

  if (digitalRead(RED_BUTTON) == LOW || keyPress == 'R') {
    setColorMessage(RED_LED);
    setFlashLight(RED_LED, HOLD_ON);
    setDisplayMessage("NEXT COLOR","");

    return RED_LED;
  }

  if (digitalRead(GREEN_BUTTON) == LOW || keyPress == 'G') {
    setColorMessage(GREEN_LED);
    setFlashLight(GREEN_LED, HOLD_ON);
    setDisplayMessage("NEXT COLOR","");

    return GREEN_LED;
  }

  if (digitalRead(BLUE_BUTTON) == LOW || keyPress == 'B') {
    setColorMessage(BLUE_LED);
    setFlashLight(BLUE_LED, HOLD_ON);
    setDisplayMessage("NEXT COLOR","");

    return BLUE_LED;
  }

  if (digitalRead(YELLOW_BUTTON) == LOW || keyPress == 'Y') {
    setColorMessage(YELLOW_LED);
    setFlashLight(YELLOW_LED, HOLD_ON);
    setDisplayMessage("NEXT COLOR","");

    return YELLOW_LED;
  }

  return UNDEFINIED;
}

void playRoundSequence() {
  for (int i = 0; i < roundPlayer; i++) {
    setDisplaySegment(i+1);

    setColorMessage(gameSet[i]);

    setFlashLight(gameSet[i], HOLD_ON);

    setDisplayMessage("PLAY SEQUENCE","");
  }
}

void setRoundPlayer() {
  roundPlayer++;
  rightAnswer = 0;

  if (roundPlayer <= MAX_SEQUENCE) {
    playRoundSequence();
  }
}

void setRightAnswer() {
  int answer = getButtonPressed();

  if (answer == UNDEFINIED) {
    return;
  }

  if (answer == gameSet[rightAnswer]) {
    rightAnswer++;
  } else {
    roundPlayer = MAX_SEQUENCE + 2;
  }
}

int getStatusGame() {
  if (roundPlayer <= MAX_SEQUENCE) {
    if (rightAnswer == roundPlayer) {
      return READY_TO_PLAY;
    } else {
      return WAITING_RESPONSE;
    }
  } else if (roundPlayer == MAX_SEQUENCE + 1) {
    return YOU_WIN;
  } else {
    return GAME_OVER;
  }
}

void welcome() {
  digitalWrite(RED_LED, HIGH);
  digitalWrite(GREEN_LED, HIGH);
  digitalWrite(BLUE_LED, HIGH);
  digitalWrite(YELLOW_LED, HIGH);

  delay(400);

  digitalWrite(RED_LED, LOW);
  digitalWrite(GREEN_LED, LOW);
  digitalWrite(BLUE_LED, LOW);
  digitalWrite(YELLOW_LED, LOW);

  delay(400);
}

void congratulation() {
  setDisplayMessage("YOU WIN","Congratulations!");

  for (int i = 0; i < MAX_SEQUENCE + 1; i++) {
    setFlashLight(gameSet[i], 200);

    setDisplaySegment(MAX_SEQUENCE);
  }

  newGame();
}

void fail() {
  setDisplayMessage("YOU LOOSE!","Try Again...");

  setPlayTone(2048, 256);

  digitalWrite(RED_LED, HIGH);
  digitalWrite(GREEN_LED, HIGH);
  digitalWrite(BLUE_LED, HIGH);
  digitalWrite(YELLOW_LED, HIGH);

  setDisplaySegment(0);

  delay(300);

  newGame();
}

void newGame() {
  roundPlayer = 0;
  rightAnswer = 0;

  randomSeed(analogRead(A7));

  for (int i = 0; i < MAX_SEQUENCE; i++) {
    gameSet[i] = random(BLUE_LED, YELLOW_LED + 1);
  }

  welcome();
}

void setup() {
  Serial.begin(9600);

  analogReference(INTERNAL);

  pinMode(RED_BUTTON, INPUT_PULLUP);
  pinMode(GREEN_BUTTON, INPUT_PULLUP);
  pinMode(BLUE_BUTTON, INPUT_PULLUP);
  pinMode(YELLOW_BUTTON, INPUT_PULLUP);

  pinMode(RED_LED, OUTPUT);
  pinMode(GREEN_LED, OUTPUT);
  pinMode(BLUE_LED, OUTPUT);
  pinMode(YELLOW_LED, OUTPUT);

  pinMode(BINARY_SEGMENT1, OUTPUT);
  pinMode(BINARY_SEGMENT2, OUTPUT);
  pinMode(BINARY_SEGMENT3, OUTPUT);
  pinMode(BINARY_SEGMENT4, OUTPUT);

  pinMode(DEFAULT_BUZZER, OUTPUT);

  lcd.begin (16, 2);

  setDisplayMessage("WELCOME GAMER","decade.com.br");

  newGame();
}

void loop() {
  if (map(analogRead(LDR), 0, 1023, 0, 100) < 50) {
    lcd.setBacklight(HIGH);
  } else {
    lcd.setBacklight(LOW);
  }

  switch (getStatusGame()) {
    case READY_TO_PLAY:
      setRoundPlayer();
      break;
    case WAITING_RESPONSE:
      setRightAnswer();
      break;
    case YOU_WIN:
      congratulation();
      break;
    case GAME_OVER:
      fail();
      break;
  }
}
